# Fritzing sketch Arbenit_Sketch (saved by Fritzing 0.9.3b)
breadboards: 1

parts:
  Bauteil1 = Arduino Uno (Rev3)
  S1 = Taiway 100-SP-X-T1 SPDT Miniature Toggle Switch [part_number=100-SP-X-T1-0-0-B1-M1 package=THT]
  S2 = Pushbutton [package="[THT]"]
  R1 = Resistor [tolerance=±5% resistance=10k package="0402 [SMD]"]
  LED1 = LED - 5mm [color="Yellow (595nm)" package="5 mm [THT]"]
  LED2 = LED - 5mm [color="Green (555nm)" package="5 mm [THT]"]
  S3 = Pushbutton [package="[THT]"]
  R2 = Resistor [tolerance=±5% resistance=10k package="0402 [SMD]"]
  LED3 = LED - 5mm [color="Green (555nm)" package="5 mm [THT]"]
  LED4 = LED - 5mm [color="Red (633nm)" package="5 mm [THT]"]
  S4 = Pushbutton [package="[THT]"]
  R3 = Resistor [tolerance=±5% resistance=10k package="0402 [SMD]"]
  LED5 = LED - 5mm [color="Red (633nm)" package="5 mm [THT]"]
  LED6 = LED - 5mm [color="Yellow (595nm)" package="5 mm [THT]"]

nets:
  N1: Bauteil1.A5/SCL, S1.COM
  N2: Bauteil1.D8, S2.Pin_3, S2.Pin_4, R1.Pin_0
  N3: Bauteil1.D9_PWM, LED1.anode, LED2.anode
  N4: Bauteil1.D2, S4.Pin_3, S4.Pin_4, R3.Pin_0
  N5: Bauteil1.D3_PWM, LED5.anode, LED6.anode
  N6: Bauteil1.D4, S3.Pin_3, S3.Pin_4, R2.Pin_0
  N7: Bauteil1.D5_PWM, LED3.anode, LED4.anode
  N8: Bauteil1.5V, S1.L2, R1.Pin_1, R2.Pin_1, R3.Pin_1
  N9: Bauteil1.GND, S1.L1, S2.Pin_1, S2.Pin_2, LED1.cathode, LED2.cathode, S3.Pin_1, S3.Pin_2, LED3.cathode, LED4.cathode, S4.Pin_1, S4.Pin_2, LED5.cathode, LED6.cathode
